# Fritzing sketch fiens-lights (saved by Fritzing 1.0.6)
breadboards: 1

parts:
  Part1 = Arduino Nano (Rev3.0) (ICSP)
  R1 = Rotary Potentiometer (Small) [maximum_resistance=10kΩ knob_status=50% power=0.5W package=THT]
  R2 = Rotary Potentiometer (Small) [maximum_resistance=10kΩ knob_status=50% power=0.5W package=THT]
  R3 = Rotary Potentiometer (Small) [maximum_resistance=10kΩ knob_status=50% power=0.5W package=THT]
  R4 = Resistor [tolerance=±5% resistance=470 package="1206 [SMD]"]
  C2 = Electrolytic Capacitor [capacitance=1mF voltage=35V package="100 mil [THT, electrolytic]"]
  S1 = Pushbutton [package="[THT]"]
  RGB_SMD_LED1 = SMD RGB LED (WS2812) [package=5050]
  RGB_SMD_LED2 = SMD RGB LED (WS2812) [package=5050]
  RGB_SMD_LED3 = SMD RGB LED (WS2812) [package=5050]

nets:
  N1: Part1.GND, R1.leg1, R2.leg1, R3.leg1, C2.+, S1.Pin_1, S1.Pin_2, RGB_SMD_LED1.DOut
  N2: Part1.D6, R4.Pin_0
  5V: Part1.5V, R1.leg2, R2.leg2, R3.leg2, C2.-, RGB_SMD_LED1.VCC
  N3: Part1.A2, R3.wiper
  N4: Part1.A1, R2.wiper
  N5: Part1.A0, R1.wiper
  N6: Part1.D13/SCK, S1.Pin_3, S1.Pin_4
  N7: R4.Pin_1, RGB_SMD_LED1.DIn
  N8: RGB_SMD_LED1.NC, RGB_SMD_LED2.VCC
  N9: RGB_SMD_LED1.VDD, RGB_SMD_LED2.DIn
  N10: RGB_SMD_LED1.VSS, RGB_SMD_LED2.DOut
  N11: RGB_SMD_LED2.NC, RGB_SMD_LED3.VCC
  N12: RGB_SMD_LED2.VDD, RGB_SMD_LED3.DIn
  N13: RGB_SMD_LED2.VSS, RGB_SMD_LED3.DOut

// code stored in the sketch: Untitled.ino

